# Fritzing sketch Verkabelung (saved by Fritzing 0.9.4)
breadboards: 1

parts:
  HC-SR04_Sensor_1 = HC-SR04 Ultrasonic Distance Sensor
  U2 = NodeMCU V3.0
  VCC1 = 4 x AAA Battery Mount
  LED1 = smd LED [color="Red (633nm)" package="1206 [SMD]"]
  R1 = Resistor [tolerance=±5% resistance=220 package="2512 [SMD]"]

nets:
  N1: HC-SR04_Sensor_1.VCC, U2.D5
  N2: HC-SR04_Sensor_1.TRIG, U2.D1
  N3: HC-SR04_Sensor_1.ECHO, U2.D2
  N4: HC-SR04_Sensor_1.GND, U2.GND#6, U2.GND#13, U2.GND#16, U2.GND#33, VCC1.-, R1.Pin_0
  N5: U2.D8, LED1.anode
  N6: U2.Vin, VCC1.+
  N7: LED1.cathode, R1.Pin_1

custom parts:
  NodeMCU V3.0: ESP8266 based NodeMCU
